// Logisim project ContadorGrayy.circ as structural Verilog: 1 circuit, main circuit main
module main (
  input  in_1,
  output out_2,
  output out_3,
  output out_4,
  output out_5
);

  wire and_1_out, and_2_out, and_3_out, and_4_out, and_5_out, and_6_out, and_7_out, and_8_out, and_9_out,
       and_10_out, and_11_out, and_12_out, and_13_out, and_14_out, and_15_out, and_16_out, F0_qn, F1_qn,
       F2_qn, F3_qn, or_1_out, or_2_out, or_3_out, or_4_out;

  J_K_Flip_Flop F0 (.J(or_1_out), .K(or_3_out), .clk(in_1), .Q(out_5), .Qn(F0_qn));  // open: preset, reset
  J_K_Flip_Flop F1 (.J(or_2_out), .K(or_4_out), .clk(in_1), .Q(out_4), .Qn(F1_qn), .reset(or_2_out));  // open: preset
  J_K_Flip_Flop F2 (.J(and_6_out), .K(and_14_out), .clk(in_1), .Q(out_3), .Qn(F2_qn));  // open: preset, reset
  J_K_Flip_Flop F3 (.J(and_7_out), .K(and_15_out), .clk(in_1), .Q(out_2), .Qn(F3_qn));  // open: preset, reset
  and and_1 (and_1_out, F3_qn, F2_qn, F1_qn);
  and and_2 (and_2_out, out_2, F2_qn, out_4);
  and and_3 (and_3_out, F3_qn, out_3, out_4);
  or or_1 (or_1_out, and_1_out, and_3_out, and_2_out, and_8_out);
  and and_4 (and_4_out, out_2, out_3, out_5, F1_qn);
  and and_5 (and_5_out, F3_qn, F2_qn, out_5);
  or or_2 (or_2_out, and_5_out, and_4_out);
  and and_6 (and_6_out, F3_qn, F2_qn, out_4, F0_qn);
  and and_7 (and_7_out, F3_qn, F1_qn, F0_qn, out_3);
  and and_8 (and_8_out, out_2, out_3, F1_qn);
  and and_9 (and_9_out, F3_qn, F2_qn, out_4);
  and and_10 (and_10_out, F3_qn, out_3, out_5);
  and and_11 (and_11_out, out_2, F2_qn, F1_qn);
  and and_12 (and_12_out, F3_qn, out_3, F1_qn);
  or or_3 (or_3_out, and_9_out, and_12_out, and_11_out, and_16_out);
  and and_13 (and_13_out, out_2, out_5, F2_qn);
  or or_4 (or_4_out, and_10_out, and_13_out);
  and and_14 (and_14_out, out_2, out_4, F0_qn);
  and and_15 (and_15_out, F2_qn, F1_qn, F0_qn);
  and and_16 (and_16_out, out_2, out_3, out_4);
endmodule
